# Fritzing sketch arduino radar (saved by Fritzing 0.9.3b)
breadboards: 1

parts:
  Part1 = Arduino Nano (Rev3.0)
  HC-SR04_Sensor_1 = HC-SR04 Ultrasonic Distance Sensor
  J1 = Basic Servo
  J2 = Dagu DGServo 9g header (male) [package=THT]
  J3 = Dagu DGServo 9g header (male) [package=THT]
  Part2 = Bluetooth HC-05 Macho

nets:
  N1: Part1.D1/TX, Part2.RXD
  N2: Part1.D0/RX, Part2.TXD
  N3: Part1.D2, HC-SR04_Sensor_1.TRIG
  N4: Part1.D3, HC-SR04_Sensor_1.ECHO
  N5: Part1.D5, J2.gnd
  N6: Part1.D6, J3.gnd
  GND: Part1.GND, HC-SR04_Sensor_1.GND
  VCC: Part1.5V, HC-SR04_Sensor_1.VCC, J1.vcc

notes:
  PWM 5 , 6
  Radar Sweep Servo
  Ultrasonic
  HC05 57600 Baud
